// Logisim project МКНФ.circ as structural Verilog: 1 circuit, main circuit main
module main (
);

  wire and_1_out, and_2_out, and_3_out, and_4_out, not_1_out, not_2_out, not_3_out, not_4_out, not_5_out,
       not_6_out, not_7_out, not_8_out, not_9_out, not_10_out, or_1_out, or_2_out, or_3_out, or_4_out,
       or_5_out, or_6_out, or_7_out, or_8_out, or_9_out, or_10_out, or_11_out, x0_out, x1_out, x2_out, x3_out;

  Clock #(.highDuration(8), .lowDuration(8)) x3 (.out(x3_out));
  Clock #(.highDuration(4), .lowDuration(4)) x2 (.out(x2_out));
  Clock #(.highDuration(2), .lowDuration(2)) x1 (.out(x1_out));
  Clock x0 (.out(x0_out));
  or or_1 (or_1_out, x2_out, not_1_out);
  not not_1 (not_1_out, x1_out);
  not not_2 (not_2_out, x0_out);
  not not_3 (not_3_out, x2_out);
  or or_2 (or_2_out, not_3_out, x1_out);
  not not_4 (not_4_out, x0_out);
  not not_5 (not_5_out, x2_out);
  not not_6 (not_6_out, x1_out);
  not not_7 (not_7_out, x3_out);
  not not_8 (not_8_out, x3_out);
  not not_9 (not_9_out, x2_out);
  or or_3 (or_3_out, or_1_out, not_2_out);
  or or_4 (or_4_out, or_2_out, not_4_out);
  or or_5 (or_5_out, not_5_out, not_6_out);
  or or_6 (or_6_out, not_7_out, x2_out);
  or or_7 (or_7_out, x1_out, x0_out);
  or or_8 (or_8_out, not_8_out, not_9_out);
  not not_10 (not_10_out, x1_out);
  and and_1 (and_1_out, or_3_out, or_4_out);
  or or_9 (or_9_out, or_5_out, x0_out);
  or or_10 (or_10_out, or_6_out, or_7_out);
  or or_11 (or_11_out, or_8_out, not_10_out);
  and and_2 (and_2_out, and_1_out, or_9_out);
  and and_3 (and_3_out, or_10_out, or_11_out);
  LED led_1 (.in(and_4_out));
  and and_4 (and_4_out, and_2_out, and_3_out);
endmodule
